// Logisim project Lofisim_P0_CRC.circ as structural Verilog: 2 circuits, main circuit CRC
module CRC (
  input  [7:0] A,
  input  [3:0] B,
  output [10:0] C
);

  wire [2:0] basic_crc_1_remainer, basic_crc_2_remainer, basic_crc_3_remainer, basic_crc_4_remainer,
       basic_crc_6_remainer, basic_crc_7_remainer;
  wire [3:1] basic_crc_5_remainer;

  Basic_crc basic_crc_1 (.dividend(A[7:4]), .divisor(B), .remainer(basic_crc_1_remainer));  // open: quotient
  Basic_crc basic_crc_2 (
    .dividend({basic_crc_1_remainer, A[3]}), .divisor(B), .remainer(basic_crc_2_remainer));  // open: quotient
  Basic_crc basic_crc_3 (
    .dividend({basic_crc_2_remainer, A[2]}), .divisor(B), .remainer(basic_crc_3_remainer));  // open: quotient
  Basic_crc basic_crc_4 (
    .dividend({basic_crc_3_remainer, A[1]}), .divisor(B), .remainer(basic_crc_4_remainer));  // open: quotient
  Basic_crc basic_crc_5 (
    .dividend({basic_crc_4_remainer, A[0]}), .divisor(B), .remainer(basic_crc_5_remainer));  // open: quotient
  Basic_crc basic_crc_6 (
    .dividend({basic_crc_5_remainer, 1'b0}), .divisor(B), .remainer(basic_crc_6_remainer));  // open: quotient
  Basic_crc basic_crc_7 (
    .dividend({basic_crc_6_remainer, 1'b0}), .divisor(B), .remainer(basic_crc_7_remainer));  // open: quotient
  Basic_crc basic_crc_8 (.dividend({basic_crc_7_remainer, 1'b0}), .divisor(B), .remainer(C[2:0]));  // open: quotient

  assign C[10:3] = A;
endmodule

module Basic_crc (
  input  [3:0] dividend,
  input  [3:0] divisor,
  output quotient,
  output [2:0] remainer
);

  wire [3:0] xor_1_out;
  wire [3:3] multiplexer_1_out;

  BitSelector #(.width(4)) bitselector_1 (.in(dividend), .out(quotient), .sel(2'b11));
  assign xor_1_out = dividend ^ divisor;  // XOR_Gate xor_1, 4 bits wide
  Multiplexer #(.width(4)) multiplexer_1 (
    .in0(dividend), .in1(xor_1_out), .out({multiplexer_1_out[3], remainer}), .sel(quotient));  // open: en
endmodule
