// Logisim project Lofisim_P0_GRF.circ as structural Verilog: 4 circuits, main circuit reset
module grf (
  input  [4:0] A1,
  input  [4:0] A2,
  input  [4:0] A3,
  input  [31:0] WD,
  input  reset,
  input  clk,
  input  WE,
  output [31:0] RD1,
  output [31:0] RD2
);

  wire [31:0] R1, R2, R3, R4, R5, R6, R7, R8, R9, R10, R11, R12, R13, R14, R15, R16, R17, R18, R19, R20, R21,
       R22, R23, R24, R25, R26, R27, R28, R29, R30, R31, W0, W1, W2, W3, W4, W5, W6, W7, W8, W9, W10, W11,
       W12, W13, W14, W15, W16, W17, W18, W19, W20, W21, W22, W23, W24, W25, W26, W27, W28, W29, W30, W31;

  write_demul_32 W (
    .out_4(W0), .out_5(W1), .out_6(W2), .out_7(W3), .out_8(W4), .out_9(W5), .out_10(W6), .out_11(W7),
    .out_12(W8), .out_13(W9), .out_14(W10), .out_15(W11), .out_16(W12), .out_17(W13), .out_18(W14),
    .out_19(W15), .out_20(W16), .out_21(W17), .out_22(W18), .out_23(W19), .out_24(W20), .out_25(W21),
    .out_26(W22), .out_27(W23), .out_28(W24), .out_29(W25), .out_30(W26), .out_31(W27), .out_32(W28),
    .out_33(W29), .out_34(W30), .out_35(W31), .input_addr(A3), .Enable(WE), .input_data(WD));
  reset register (
    .in_1(W0), .in_2(W1), .in_3(W2), .in_4(W3), .in_5(W4), .in_6(W5), .in_7(W6), .in_8(W7), .in_9(W8),
    .in_10(W9), .in_11(W10), .in_12(W11), .in_13(W12), .in_14(W13), .in_15(W14), .in_16(W15), .in_17(W16),
    .in_18(W17), .in_19(W18), .in_20(W19), .in_21(W20), .in_22(W21), .in_23(W22), .in_24(W23), .in_25(W24),
    .in_26(W25), .in_27(W26), .in_28(W27), .in_29(W28), .in_30(W29), .in_31(W30), .in_32(W31), .enable(WE),
    .clk(clk), .reset(reset), .out_37(R1), .out_38(R2), .out_39(R3), .out_40(R4), .out_41(R5), .out_42(R6),
    .out_43(R7), .out_44(R8), .out_45(R9), .out_46(R10), .out_47(R11), .out_48(R12), .out_49(R13),
    .out_50(R14), .out_51(R15), .out_52(R16), .out_53(R17), .out_54(R18), .out_55(R19), .out_56(R20),
    .out_57(R21), .out_58(R22), .out_59(R23), .out_60(R24), .out_61(R25), .out_62(R26), .out_63(R27),
    .out_64(R28), .out_65(R29), .out_66(R30), .out_67(R31));  // open: out_36
  read_mul_32 u_R1 (
    .in_1(R1), .in_2(R2), .in_3(R3), .in_4(R4), .in_5(R5), .in_6(R6), .in_7(R7), .in_8(R8), .in_9(R9),
    .in_10(R10), .in_11(R11), .in_12(R12), .in_13(R13), .in_14(R14), .in_15(R15), .in_16(R16), .in_17(R17),
    .in_18(R18), .in_19(R19), .in_20(R20), .in_21(R21), .in_22(R22), .in_23(R23), .in_24(R24), .in_25(R25),
    .in_26(R26), .in_27(R27), .in_28(R28), .in_29(R29), .in_30(R30), .in_31(R31), .input_addr(A1),
    .output_data(RD1));
  read_mul_32 u_R2 (
    .in_1(R1), .in_2(R2), .in_3(R3), .in_4(R4), .in_5(R5), .in_6(R6), .in_7(R7), .in_8(R8), .in_9(R9),
    .in_10(R10), .in_11(R11), .in_12(R12), .in_13(R13), .in_14(R14), .in_15(R15), .in_16(R16), .in_17(R17),
    .in_18(R18), .in_19(R19), .in_20(R20), .in_21(R21), .in_22(R22), .in_23(R23), .in_24(R24), .in_25(R25),
    .in_26(R26), .in_27(R27), .in_28(R28), .in_29(R29), .in_30(R30), .in_31(R31), .input_addr(A2),
    .output_data(RD2));
endmodule

module read_mul_32 (
  input  [31:0] in_1,
  input  [31:0] in_2,
  input  [31:0] in_3,
  input  [31:0] in_4,
  input  [31:0] in_5,
  input  [31:0] in_6,
  input  [31:0] in_7,
  input  [31:0] in_8,
  input  [31:0] in_9,
  input  [31:0] in_10,
  input  [31:0] in_11,
  input  [31:0] in_12,
  input  [31:0] in_13,
  input  [31:0] in_14,
  input  [31:0] in_15,
  input  [31:0] in_16,
  input  [31:0] in_17,
  input  [31:0] in_18,
  input  [31:0] in_19,
  input  [31:0] in_20,
  input  [31:0] in_21,
  input  [31:0] in_22,
  input  [31:0] in_23,
  input  [31:0] in_24,
  input  [31:0] in_25,
  input  [31:0] in_26,
  input  [31:0] in_27,
  input  [31:0] in_28,
  input  [31:0] in_29,
  input  [31:0] in_30,
  input  [31:0] in_31,
  input  [4:0] input_addr,
  output [31:0] output_data
);

  Multiplexer #(.select(5), .width(32)) multiplexer_1 (
    .in0({32{1'b0}}), .in1(in_1), .in2(in_2), .in3(in_3), .in4(in_4), .in5(in_5), .in6(in_6), .in7(in_7),
    .in8(in_8), .in9(in_9), .in10(in_10), .in11(in_11), .in12(in_12), .in13(in_13), .in14(in_14),
    .in15(in_15), .in16(in_16), .in17(in_17), .in18(in_18), .in19(in_19), .in20(in_20), .in21(in_21),
    .in22(in_22), .in23(in_23), .in24(in_24), .in25(in_25), .in26(in_26), .in27(in_27), .in28(in_28),
    .in29(in_29), .in30(in_30), .in31(in_31), .out(output_data), .sel(input_addr));  // open: en
endmodule

module reset (
  input  [31:0] in_1,
  input  [31:0] in_2,
  input  [31:0] in_3,
  input  [31:0] in_4,
  input  [31:0] in_5,
  input  [31:0] in_6,
  input  [31:0] in_7,
  input  [31:0] in_8,
  input  [31:0] in_9,
  input  [31:0] in_10,
  input  [31:0] in_11,
  input  [31:0] in_12,
  input  [31:0] in_13,
  input  [31:0] in_14,
  input  [31:0] in_15,
  input  [31:0] in_16,
  input  [31:0] in_17,
  input  [31:0] in_18,
  input  [31:0] in_19,
  input  [31:0] in_20,
  input  [31:0] in_21,
  input  [31:0] in_22,
  input  [31:0] in_23,
  input  [31:0] in_24,
  input  [31:0] in_25,
  input  [31:0] in_26,
  input  [31:0] in_27,
  input  [31:0] in_28,
  input  [31:0] in_29,
  input  [31:0] in_30,
  input  [31:0] in_31,
  input  [31:0] in_32,
  input  reset,
  input  clk,
  input  enable,
  output [31:0] out_36,
  output [31:0] out_37,
  output [31:0] out_38,
  output [31:0] out_39,
  output [31:0] out_40,
  output [31:0] out_41,
  output [31:0] out_42,
  output [31:0] out_43,
  output [31:0] out_44,
  output [31:0] out_45,
  output [31:0] out_46,
  output [31:0] out_47,
  output [31:0] out_48,
  output [31:0] out_49,
  output [31:0] out_50,
  output [31:0] out_51,
  output [31:0] out_52,
  output [31:0] out_53,
  output [31:0] out_54,
  output [31:0] out_55,
  output [31:0] out_56,
  output [31:0] out_57,
  output [31:0] out_58,
  output [31:0] out_59,
  output [31:0] out_60,
  output [31:0] out_61,
  output [31:0] out_62,
  output [31:0] out_63,
  output [31:0] out_64,
  output [31:0] out_65,
  output [31:0] out_66,
  output [31:0] out_67
);

  Register #(.width(32)) _0 (.D(in_1), .en(enable), .Q(out_36), .clk(clk), .clr(reset));
  Register #(.width(32)) _4 (.D(in_5), .en(enable), .Q(out_40), .clk(clk), .clr(reset));
  Register #(.width(32)) _8 (.D(in_9), .en(enable), .Q(out_44), .clk(clk), .clr(reset));
  Register #(.width(32)) _12 (.D(in_13), .en(enable), .Q(out_48), .clk(clk), .clr(reset));
  Register #(.width(32)) _16 (.D(in_17), .en(enable), .Q(out_52), .clk(clk), .clr(reset));
  Register #(.width(32)) _20 (.D(in_21), .en(enable), .Q(out_56), .clk(clk), .clr(reset));
  Register #(.width(32)) _24 (.D(in_25), .en(enable), .Q(out_60), .clk(clk), .clr(reset));
  Register #(.width(32)) _28 (.D(in_29), .en(enable), .Q(out_64), .clk(clk), .clr(reset));
  Register #(.width(32)) _1 (.D(in_2), .en(enable), .Q(out_37), .clk(clk), .clr(reset));
  Register #(.width(32)) _5 (.D(in_6), .en(enable), .Q(out_41), .clk(clk), .clr(reset));
  Register #(.width(32)) _9 (.D(in_10), .en(enable), .Q(out_45), .clk(clk), .clr(reset));
  Register #(.width(32)) _13 (.D(in_14), .en(enable), .Q(out_49), .clk(clk), .clr(reset));
  Register #(.width(32)) _17 (.D(in_18), .en(enable), .Q(out_53), .clk(clk), .clr(reset));
  Register #(.width(32)) _21 (.D(in_22), .en(enable), .Q(out_57), .clk(clk), .clr(reset));
  Register #(.width(32)) _25 (.D(in_26), .en(enable), .Q(out_61), .clk(clk), .clr(reset));
  Register #(.width(32)) _29 (.D(in_30), .en(enable), .Q(out_65), .clk(clk), .clr(reset));
  Register #(.width(32)) _2 (.D(in_3), .en(enable), .Q(out_38), .clk(clk), .clr(reset));
  Register #(.width(32)) _6 (.D(in_7), .en(enable), .Q(out_42), .clk(clk), .clr(reset));
  Register #(.width(32)) _10 (.D(in_11), .en(enable), .Q(out_46), .clk(clk), .clr(reset));
  Register #(.width(32)) _14 (.D(in_15), .en(enable), .Q(out_50), .clk(clk), .clr(reset));
  Register #(.width(32)) _18 (.D(in_19), .en(enable), .Q(out_54), .clk(clk), .clr(reset));
  Register #(.width(32)) _22 (.D(in_23), .en(enable), .Q(out_58), .clk(clk), .clr(reset));
  Register #(.width(32)) _26 (.D(in_27), .en(enable), .Q(out_62), .clk(clk), .clr(reset));
  Register #(.width(32)) _30 (.D(in_31), .en(enable), .Q(out_66), .clk(clk), .clr(reset));
  Register #(.width(32)) _3 (.D(in_4), .en(enable), .Q(out_39), .clk(clk), .clr(reset));
  Register #(.width(32)) _7 (.D(in_8), .en(enable), .Q(out_43), .clk(clk), .clr(reset));
  Register #(.width(32)) _11 (.D(in_12), .en(enable), .Q(out_47), .clk(clk), .clr(reset));
  Register #(.width(32)) _15 (.D(in_16), .en(enable), .Q(out_51), .clk(clk), .clr(reset));
  Register #(.width(32)) _19 (.D(in_20), .en(enable), .Q(out_55), .clk(clk), .clr(reset));
  Register #(.width(32)) _23 (.D(in_24), .en(enable), .Q(out_59), .clk(clk), .clr(reset));
  Register #(.width(32)) _27 (.D(in_28), .en(enable), .Q(out_63), .clk(clk), .clr(reset));
  Register #(.width(32)) _31 (.D(in_32), .en(enable), .Q(out_67), .clk(clk), .clr(reset));
endmodule

module write_demul_32 (
  input  [31:0] input_data,
  input  [4:0] input_addr,
  input  Enable,
  output [31:0] out_4,
  output [31:0] out_5,
  output [31:0] out_6,
  output [31:0] out_7,
  output [31:0] out_8,
  output [31:0] out_9,
  output [31:0] out_10,
  output [31:0] out_11,
  output [31:0] out_12,
  output [31:0] out_13,
  output [31:0] out_14,
  output [31:0] out_15,
  output [31:0] out_16,
  output [31:0] out_17,
  output [31:0] out_18,
  output [31:0] out_19,
  output [31:0] out_20,
  output [31:0] out_21,
  output [31:0] out_22,
  output [31:0] out_23,
  output [31:0] out_24,
  output [31:0] out_25,
  output [31:0] out_26,
  output [31:0] out_27,
  output [31:0] out_28,
  output [31:0] out_29,
  output [31:0] out_30,
  output [31:0] out_31,
  output [31:0] out_32,
  output [31:0] out_33,
  output [31:0] out_34,
  output [31:0] out_35
);

  Demultiplexer #(.select(5), .width(32), .tristate("true")) demultiplexer_1 (
    .out0(out_4), .out1(out_5), .out2(out_6), .out3(out_7), .out4(out_8), .out5(out_9), .out6(out_10),
    .out7(out_11), .out8(out_12), .out9(out_13), .out10(out_14), .out11(out_15), .out12(out_16),
    .out13(out_17), .out14(out_18), .out15(out_19), .out16(out_20), .out17(out_21), .out18(out_22),
    .out19(out_23), .out20(out_24), .out21(out_25), .out22(out_26), .out23(out_27), .out24(out_28),
    .out25(out_29), .out26(out_30), .out27(out_31), .out28(out_32), .out29(out_33), .out30(out_34),
    .out31(out_35), .in(input_data), .sel(input_addr), .en(Enable));
endmodule
