// Logisim project Logisim_P0_FSM.circ as structural Verilog: 3 circuits, main circuit fsm
module fsm (
  input  [1:0] In,
  input  CLR,
  output Z
);

  wire clock_1_out;
  wire [1:0] multiplexer_1_out, state_change_now, state_q;

  \状态转移  state_change (.pre(state_q), .\input (In), .now(state_change_now));
  Register #(.width(2)) state (.D(multiplexer_1_out), .Q(state_q), .clk(clock_1_out));  // open: en, clr
  Multiplexer #(.width(2)) multiplexer_1 (
    .in0(state_change_now), .in1(2'b00), .out(multiplexer_1_out), .sel(CLR));  // open: en
  Clock clock_1 (.out(clock_1_out));
  Output output_1 (.state(state_q), .\input (In), .Output(Z));
endmodule

module \状态转移  (
  input  [1:0] pre,
  input  [1:0] \input ,
  output [1:0] now
);

  wire and_1_out, and_2_out, and_3_out, and_4_out, not_1_out, not_2_out, not_3_out, not_4_out, not_5_out,
       not_6_out, not_7_out;

  not not_1 (not_1_out, pre[1]);
  not not_2 (not_2_out, \input [0]);
  not not_3 (not_3_out, pre[0]);
  not not_4 (not_4_out, \input [0]);
  not not_5 (not_5_out, \input [1]);
  not not_6 (not_6_out, pre[0]);
  not not_7 (not_7_out, \input [0]);
  and and_1 (and_1_out, not_1_out, pre[0], not_2_out);
  and and_2 (and_2_out, pre[1], not_3_out, not_4_out);
  and and_3 (and_3_out, not_5_out, \input [0]);
  and and_4 (and_4_out, pre[1], not_6_out, not_7_out);
  or or_1 (now[1], and_1_out, and_2_out);
  or or_2 (now[0], and_3_out, and_4_out);
endmodule

module Output (
  input  [1:0] state,
  input  [1:0] \input ,
  output Output
);

  wire not_1_out, not_2_out;

  not not_1 (not_1_out, state[0]);
  not not_2 (not_2_out, \input [0]);
  and and_1 (Output, state[1], not_1_out, not_2_out);
endmodule
