// Logisim project Logisim_P0_navigation.circ as structural Verilog: 2 circuits, main circuit navigation
module navigation (
  input  [1:0] dir,
  input  clk,
  input  reset,
  output arrive,
  output hit
);

  wire not_1_out, \状态转移_1_arrive , \状态转移_1_hit ;
  wire [1:0] now_state_q, \状态转移_1_now_state ;

  \状态转移  \u_状态转移_1  (
    .\input (dir), .pre_state(now_state_q), .arrive_signal(arrive), .now_state(\状态转移_1_now_state ),
    .hit(\状态转移_1_hit ), .arrive(\状态转移_1_arrive ));
  not not_1 (not_1_out, arrive);
  Register #(.width(2)) now_state (.D(\状态转移_1_now_state ), .en(not_1_out), .Q(now_state_q), .clk(clk), .clr(reset));
  Register #(.width(1)) u_hit (.D(\状态转移_1_hit ), .en(not_1_out), .Q(hit), .clk(clk), .clr(reset));
  Register #(.width(1)) u_arrive (.D(\状态转移_1_arrive ), .Q(arrive), .clk(clk), .clr(reset));  // open: en
endmodule

module \状态转移  (
  input  [1:0] \input ,
  input  [1:0] pre_state,
  input  arrive_signal,
  output [1:0] now_state,
  output hit,
  output arrive
);

  wire and_1_out, and_2_out, and_3_out, and_4_out, and_5_out, and_6_out, and_7_out, and_8_out, and_9_out,
       and_10_out, and_11_out, and_12_out, and_13_out, and_14_out, and_15_out, and_16_out, not_1_out,
       not_2_out, not_3_out, not_4_out, not_5_out, not_6_out, not_7_out, not_8_out, not_9_out, not_10_out,
       not_11_out, not_12_out, not_13_out, not_14_out, not_15_out, not_16_out, not_17_out, not_18_out,
       not_19_out, not_20_out, not_21_out, not_22_out, not_23_out, not_24_out, pre_0, pre_1;

  Multiplexer #(.width(2)) multiplexer_1 (
    .in0(pre_state), .in1(2'b00), .out({pre_1, pre_0}), .sel(arrive_signal));  // open: en
  not not_1 (not_1_out, pre_1);
  not not_2 (not_2_out, \input [1]);
  not not_3 (not_3_out, \input [1]);
  not not_4 (not_4_out, \input [0]);
  not not_5 (not_5_out, pre_0);
  not not_6 (not_6_out, \input [1]);
  not not_7 (not_7_out, pre_0);
  not not_8 (not_8_out, \input [0]);
  not not_9 (not_9_out, pre_1);
  not not_10 (not_10_out, \input [1]);
  not not_11 (not_11_out, \input [0]);
  not not_12 (not_12_out, \input [0]);
  not not_13 (not_13_out, pre_0);
  not not_14 (not_14_out, \input [1]);
  not not_15 (not_15_out, pre_1);
  not not_16 (not_16_out, pre_0);
  not not_17 (not_17_out, pre_0);
  not not_18 (not_18_out, \input [0]);
  not not_19 (not_19_out, \input [1]);
  not not_20 (not_20_out, \input [0]);
  not not_21 (not_21_out, pre_0);
  not not_22 (not_22_out, \input [1]);
  not not_23 (not_23_out, \input [0]);
  not not_24 (not_24_out, \input [1]);
  and and_1 (and_1_out, not_1_out, pre_0, not_2_out);
  and and_2 (and_2_out, pre_0, not_3_out, not_4_out);
  and and_3 (and_3_out, pre_1, not_5_out, not_6_out, \input [0]);
  and and_4 (and_4_out, pre_1, not_7_out, \input [1], not_8_out);
  and and_5 (and_5_out, pre_1, pre_0, \input [1], \input [0]);
  and and_6 (and_6_out, not_9_out, not_10_out, not_11_out);
  and and_7 (and_7_out, pre_0, \input [1], \input [0]);
  and and_8 (and_8_out, pre_1, \input [1], \input [0]);
  and and_9 (and_9_out, pre_1, pre_0, not_12_out);
  and and_10 (and_10_out, not_13_out, not_14_out, \input [0]);
  and and_11 (and_11_out, not_15_out, not_16_out, \input [1]);
  and and_12 (and_12_out, not_17_out, \input [1], not_18_out);
  and and_13 (and_13_out, pre_0, \input [1], \input [0]);
  and and_14 (and_14_out, pre_1, pre_0, not_19_out, not_20_out);
  and and_15 (and_15_out, pre_1, not_21_out, not_22_out, not_23_out);
  and and_16 (and_16_out, pre_1, pre_0, not_24_out, \input [0]);
  or or_1 (now_state[1], and_1_out, and_2_out, and_3_out, and_4_out, and_5_out);
  or or_2 (now_state[0], and_6_out, and_7_out, and_8_out, and_9_out);
  or or_3 (hit, and_10_out, and_11_out, and_12_out, and_13_out, and_14_out);
  or or_4 (arrive, and_15_out, and_16_out);

  // Other names for the same wires on the sheet: input_0 = \input [0]; input_1 = \input [1]; now_0 = now_state[0];
  //   now_1 = now_state[1]
endmodule
