// Logisim project Logisim_单周期CPU.circ as structural Verilog: 8 circuits, main circuit main
module main (
  input  in_1,
  output [31:0] Instr,
  output [31:0] PC,
  output RegWrite,
  output [4:0] RegAddr,
  output [31:0] RegData,
  output MemWrite,
  output [31:0] MemAddr,
  output [31:0] MemData
);

  wire alu_1_zero, clk, controller_1_alusrc, controller_1_extimm, controller_1_numread, controller_1_opnpc,
       controller_1_regsel, multiplexer_4_out;
  wire [1:0] controller_1_opalu;
  wire [31:0] bit_extender_1_out, bit_extender_2_out, dm_1_rd, grf_1_rd1, multiplexer_1_out,
       multiplexer_3_out, npc_1_pc_prime;

  Clock clock_1 (.out(clk));
  NPC npc_1 (.PC(PC), .Branch(multiplexer_1_out), .PC_prime(npc_1_pc_prime), .op_PC(multiplexer_4_out));
  IFU ifu_1 (.clk(clk), .Reset(in_1), .PC_prime(npc_1_pc_prime), .Instr(Instr), .PC(PC));
  Controller controller_1 (
    .opcode(Instr[31:26]), .funct(Instr[5:0]), .opALU(controller_1_opalu), .NumRead(controller_1_numread),
    .opNPC(controller_1_opnpc), .RegSel(controller_1_regsel), .ALUsrc(controller_1_alusrc),
    .RegWrite(RegWrite), .NumWrite(MemWrite), .ExtImm(controller_1_extimm));
  assign bit_extender_1_out = {{16{1'b0}}, Instr[15:0]};  // Bit_Extender bit_extender_1
  assign bit_extender_2_out = {{16{Instr[15]}}, Instr[15:0]};  // Bit_Extender bit_extender_2
  GRF grf_1 (
    .A1(Instr[25:21]), .WE(RegWrite), .clk(clk), .reset(in_1), .WD(RegData), .A3(RegAddr), .A2(Instr[20:16]),
    .RD1(grf_1_rd1), .RD2(MemData));
  Multiplexer #(.width(32), .enable("false")) multiplexer_1 (
    .in0(bit_extender_1_out), .in1(bit_extender_2_out), .out(multiplexer_1_out), .sel(controller_1_extimm));
  Multiplexer #(.width(5), .enable("false")) multiplexer_2 (
    .in0(Instr[20:16]), .in1(Instr[15:11]), .out(RegAddr), .sel(controller_1_regsel));
  Multiplexer #(.width(32), .enable("false")) multiplexer_3 (
    .in0(MemData), .in1(multiplexer_1_out), .out(multiplexer_3_out), .sel(controller_1_alusrc));
  ALU alu_1 (
    .SrcA(grf_1_rd1), .SrcB(multiplexer_3_out), .op_ALU(controller_1_opalu), .out_5(MemAddr),
    .Zero(alu_1_zero));  // open: SHF
  Multiplexer #(.enable("false")) multiplexer_4 (
    .in0(1'b0), .in1(controller_1_opnpc), .out(multiplexer_4_out), .sel(alu_1_zero));
  DM dm_1 (.addr(MemAddr), .WE(MemWrite), .clk(clk), .WD(MemData), .reset(in_1), .RD(dm_1_rd));
  Multiplexer #(.width(32), .enable("false")) multiplexer_5 (
    .in0(MemAddr), .in1(dm_1_rd), .out(RegData), .sel(controller_1_numread));

  // Other names for the same wires on the sheet: reset = in_1

  // Notes on the sheet:
  //   15:0
  //   31:26
  //   5:0
  //   25:21
  //   20:16
  //   20:16
  //   15:11
  //   EXT
endmodule

module IM (
  input  clk,
  input  Reset,
  input  [31:0] PC,
  output [31:0] Instr
);

  wire [31:0] subtractor_1_out;

  Subtractor #(.width(32)) subtractor_1 (.a(PC), .b(32'h3000), .out(subtractor_1_out));  // open: bin, bout
  ROM #(.addrWidth(12), .dataWidth(32)) rom_1 (.addr(subtractor_1_out[13:2]), .data(Instr));  // open: sel
endmodule

module NPC (
  input  [31:0] PC,
  input  [31:0] Branch,
  input  op_PC,
  output [31:0] PC_prime
);

  wire [31:0] Branch_pc, Normal_pc, shifter_1_out;

  Adder #(.width(32)) adder_1 (.a(PC), .b(32'h4), .out(Normal_pc));  // open: cin, cout
  Adder #(.width(32)) adder_2 (.a(Normal_pc), .b(shifter_1_out), .out(Branch_pc));  // open: cin, cout
  Shifter #(.width(32)) shifter_1 (.in(Branch), .\dist (5'b00010), .out(shifter_1_out));
  Multiplexer #(.width(32), .enable("false")) multiplexer_1 (
    .in0(Normal_pc), .in1(Branch_pc), .out(PC_prime), .sel(op_PC));
endmodule

module GRF (
  input  [4:0] A1,
  input  WE,
  input  clk,
  input  reset,
  input  [31:0] WD,
  input  [4:0] A3,
  input  [4:0] A2,
  output [31:0] RD1,
  output [31:0] RD2
);

  wire [31:0] In_0, In_1, In_2, In_3, In_4, In_5, In_6, In_7, In_8, In_9, In_10, In_11, In_12, In_13, In_14,
       In_15, In_16, In_17, In_18, In_19, In_20, In_21, In_22, In_23, In_24, In_25, In_26, In_27, In_28,
       In_29, In_30, In_31, Out_0, Out_1, Out_2, Out_3, Out_4, Out_5, Out_6, Out_7, Out_8, Out_9, Out_10,
       Out_11, Out_12, Out_13, Out_14, Out_15, Out_16, Out_17, Out_18, Out_19, Out_20, Out_21, Out_22,
       Out_23, Out_24, Out_25, Out_26, Out_27, Out_28, Out_29, Out_30, Out_31;

  Register #(.width(32)) _0 (.D(In_0), .en(WE), .Q(Out_0), .clk(clk), .clr(reset));
  Register #(.width(32)) _4 (.D(In_4), .en(WE), .Q(Out_4), .clk(clk), .clr(reset));
  Register #(.width(32)) _8 (.D(In_8), .en(WE), .Q(Out_8), .clk(clk), .clr(reset));
  Register #(.width(32)) _12 (.D(In_12), .en(WE), .Q(Out_12), .clk(clk), .clr(reset));
  Register #(.width(32)) _16 (.D(In_16), .en(WE), .Q(Out_16), .clk(clk), .clr(reset));
  Register #(.width(32)) _20 (.D(In_20), .en(WE), .Q(Out_20), .clk(clk), .clr(reset));
  Register #(.width(32)) _24 (.D(In_24), .en(WE), .Q(Out_24), .clk(clk), .clr(reset));
  Register #(.width(32)) _28 (.D(In_28), .en(WE), .Q(Out_28), .clk(clk), .clr(reset));
  Demultiplexer #(.select(5), .width(32), .tristate("true")) demultiplexer_1 (
    .out0(In_0), .out1(In_1), .out2(In_2), .out3(In_3), .out4(In_4), .out5(In_5), .out6(In_6), .out7(In_7),
    .out8(In_8), .out9(In_9), .out10(In_10), .out11(In_11), .out12(In_12), .out13(In_13), .out14(In_14),
    .out15(In_15), .out16(In_16), .out17(In_17), .out18(In_18), .out19(In_19), .out20(In_20), .out21(In_21),
    .out22(In_22), .out23(In_23), .out24(In_24), .out25(In_25), .out26(In_26), .out27(In_27), .out28(In_28),
    .out29(In_29), .out30(In_30), .out31(In_31), .in(WD), .sel(A3));  // open: en
  Register #(.width(32)) _1 (.D(In_1), .en(WE), .Q(Out_1), .clk(clk), .clr(reset));
  Register #(.width(32)) _5 (.D(In_5), .en(WE), .Q(Out_5), .clk(clk), .clr(reset));
  Register #(.width(32)) _9 (.D(In_9), .en(WE), .Q(Out_9), .clk(clk), .clr(reset));
  Register #(.width(32)) _13 (.D(In_13), .en(WE), .Q(Out_13), .clk(clk), .clr(reset));
  Register #(.width(32)) _17 (.D(In_17), .en(WE), .Q(Out_17), .clk(clk), .clr(reset));
  Register #(.width(32)) _21 (.D(In_21), .en(WE), .Q(Out_21), .clk(clk), .clr(reset));
  Register #(.width(32)) _25 (.D(In_25), .en(WE), .Q(Out_25), .clk(clk), .clr(reset));
  Register #(.width(32)) _29 (.D(In_29), .en(WE), .Q(Out_29), .clk(clk), .clr(reset));
  Register #(.width(32)) _2 (.D(In_2), .en(WE), .Q(Out_2), .clk(clk), .clr(reset));
  Register #(.width(32)) _6 (.D(In_6), .en(WE), .Q(Out_6), .clk(clk), .clr(reset));
  Register #(.width(32)) _10 (.D(In_10), .en(WE), .Q(Out_10), .clk(clk), .clr(reset));
  Register #(.width(32)) _14 (.D(In_14), .en(WE), .Q(Out_14), .clk(clk), .clr(reset));
  Register #(.width(32)) _18 (.D(In_18), .en(WE), .Q(Out_18), .clk(clk), .clr(reset));
  Register #(.width(32)) _22 (.D(In_22), .en(WE), .Q(Out_22), .clk(clk), .clr(reset));
  Register #(.width(32)) _26 (.D(In_26), .en(WE), .Q(Out_26), .clk(clk), .clr(reset));
  Register #(.width(32)) _30 (.D(In_30), .en(WE), .Q(Out_30), .clk(clk), .clr(reset));
  Register #(.width(32)) _3 (.D(In_3), .en(WE), .Q(Out_3), .clk(clk), .clr(reset));
  Register #(.width(32)) _7 (.D(In_7), .en(WE), .Q(Out_7), .clk(clk), .clr(reset));
  Register #(.width(32)) _11 (.D(In_11), .en(WE), .Q(Out_11), .clk(clk), .clr(reset));
  Register #(.width(32)) _15 (.D(In_15), .en(WE), .Q(Out_15), .clk(clk), .clr(reset));
  Register #(.width(32)) _19 (.D(In_19), .en(WE), .Q(Out_19), .clk(clk), .clr(reset));
  Register #(.width(32)) _23 (.D(In_23), .en(WE), .Q(Out_23), .clk(clk), .clr(reset));
  Register #(.width(32)) _27 (.D(In_27), .en(WE), .Q(Out_27), .clk(clk), .clr(reset));
  Register #(.width(32)) _31 (.D(In_31), .en(WE), .Q(Out_31), .clk(clk), .clr(reset));
  Multiplexer #(.select(5), .width(32)) multiplexer_1 (
    .in0({32{1'b0}}), .in1(Out_1), .in2(Out_2), .in3(Out_3), .in4(Out_4), .in5(Out_5), .in6(Out_6),
    .in7(Out_7), .in8(Out_8), .in9(Out_9), .in10(Out_10), .in11(Out_11), .in12(Out_12), .in13(Out_13),
    .in14(Out_14), .in15(Out_15), .in16(Out_16), .in17(Out_17), .in18(Out_18), .in19(Out_19), .in20(Out_20),
    .in21(Out_21), .in22(Out_22), .in23(Out_23), .in24(Out_24), .in25(Out_25), .in26(Out_26), .in27(Out_27),
    .in28(Out_28), .in29(Out_29), .in30(Out_30), .in31(Out_31), .out(RD1), .sel(A1));  // open: en
  Multiplexer #(.select(5), .width(32)) multiplexer_2 (
    .in0({32{1'b0}}), .in1(Out_1), .in2(Out_2), .in3(Out_3), .in4(Out_4), .in5(Out_5), .in6(Out_6),
    .in7(Out_7), .in8(Out_8), .in9(Out_9), .in10(Out_10), .in11(Out_11), .in12(Out_12), .in13(Out_13),
    .in14(Out_14), .in15(Out_15), .in16(Out_16), .in17(Out_17), .in18(Out_18), .in19(Out_19), .in20(Out_20),
    .in21(Out_21), .in22(Out_22), .in23(Out_23), .in24(Out_24), .in25(Out_25), .in26(Out_26), .in27(Out_27),
    .in28(Out_28), .in29(Out_29), .in30(Out_30), .in31(Out_31), .out(RD2), .sel(A2));  // open: en
endmodule

module ALU (
  input  [31:0] SrcA,
  input  [31:0] SrcB,
  input  [4:0] SHF,
  input  [1:0] op_ALU,
  output [31:0] out_5,
  output Zero
);

  wire [31:0] add, \or , shift, sub;

  Adder #(.width(32)) adder_1 (.a(SrcA), .b(SrcB), .out(add));  // open: cin, cout
  Subtractor #(.width(32)) subtractor_1 (.a(SrcA), .b(SrcB), .out(sub));  // open: bin, bout
  assign \or  = SrcA | SrcB;  // OR_Gate or_1, 32 bits wide
  Shifter #(.width(32)) shifter_1 (.in(SrcB), .\dist (5'b10000), .out(shift));
  Multiplexer #(.select(2), .width(32)) multiplexer_1 (
    .in0(add), .in1(sub), .in2(\or ), .in3(shift), .out(out_5), .sel(op_ALU));  // open: en
  Comparator #(.width(32), .mode("unsigned")) comparator_1 (.a(out_5), .b({32{1'b0}}), .eq(Zero));  // open: gt, lt
endmodule

module DM (
  input  [31:0] addr,
  input  WE,
  input  clk,
  input  [31:0] WD,
  input  reset,
  output [31:0] RD
);

  RAM #(.addrWidth(12), .dataWidth(32), .bus("separate")) ram_1 (
    .addr(addr[11:0]), .din(WD), .data(RD), .str(WE), .clk(clk), .ld(1'b1), .clr(reset));  // open: sel
endmodule

module Controller (
  input  [5:0] opcode,
  input  [5:0] funct,
  output NumRead,
  output NumWrite,
  output opNPC,
  output ExtImm,
  output RegSel,
  output ALUsrc,
  output RegWrite,
  output [1:0] opALU
);

  wire add, ALU_0_out, ALU_1_out, lui, not_1_out, not_2_out, not_3_out, not_4_out, not_5_out, not_6_out,
       not_7_out, not_8_out, not_9_out, not_10_out, not_11_out, not_12_out, ori, R, sub;
  wire [1:0] multiplexer_1_out, multiplexer_2_out, multiplexer_3_out;

  not not_1 (not_1_out, opcode[0]);
  not not_2 (not_2_out, opcode[1]);
  not not_3 (not_3_out, opcode[2]);
  not not_4 (not_4_out, opcode[3]);
  not not_5 (not_5_out, opcode[4]);
  not not_6 (not_6_out, opcode[5]);
  and u_R (R, not_6_out, not_5_out, not_4_out, not_3_out, not_2_out, not_1_out);
  not not_7 (not_7_out, funct[0]);
  not not_8 (not_8_out, funct[1]);
  not not_9 (not_9_out, funct[2]);
  not not_10 (not_10_out, funct[3]);
  not not_11 (not_11_out, funct[4]);
  not not_12 (not_12_out, funct[5]);
  and u_ori (ori, not_6_out, not_5_out, opcode[3], opcode[2], not_2_out, opcode[0]);
  and u_add (add, funct[5], not_11_out, not_10_out, not_9_out, not_8_out, not_7_out, R);
  and u_sub (sub, funct[5], not_11_out, not_10_out, not_9_out, funct[1], not_7_out, R);
  or u_ExtImm (ExtImm, NumRead, NumWrite, opNPC);
  and lw (NumRead, opcode[5], not_5_out, not_4_out, not_3_out, opcode[1], opcode[0]);
  or Reg_sel (RegSel, sub, add);
  and sw (NumWrite, opcode[5], not_5_out, opcode[3], not_3_out, opcode[1], opcode[0]);
  or u_ALUsrc (ALUsrc, ori, NumRead, NumWrite, lui);
  and beq (opNPC, not_6_out, not_5_out, not_4_out, opcode[2], not_2_out, not_1_out);
  or Reg_Write (RegWrite, add, sub, ori, NumRead, lui);
  and u_lui (lui, not_6_out, not_5_out, opcode[3], opcode[2], opcode[1], opcode[0]);
  or ALU_0 (ALU_0_out, add, NumRead, NumWrite);
  or ALU_1 (ALU_1_out, sub, opNPC);
  Multiplexer #(.width(2)) multiplexer_1 (.in0(2'b00), .in1(2'b11), .out(multiplexer_1_out), .sel(lui));  // open: en
  Multiplexer #(.width(2)) multiplexer_2 (
    .in0(multiplexer_1_out), .in1(2'b10), .out(multiplexer_2_out), .sel(ori));  // open: en
  Multiplexer #(.width(2)) multiplexer_3 (
    .in0(multiplexer_2_out), .in1(2'b01), .out(multiplexer_3_out), .sel(ALU_1_out));  // open: en
  Multiplexer #(.width(2)) multiplexer_4 (
    .in0(multiplexer_3_out), .in1(2'b00), .out(opALU), .sel(ALU_0_out));  // open: en

  // Other names for the same wires on the sheet: beq = opNPC; fun0 = funct[0]; fun1 = funct[1]; fun2 = funct[2];
  //   fun3 = funct[3]; fun4 = funct[4]; fun5 = funct[5]; lw = NumRead; op0 = opcode[0]; op1 = opcode[1];
  //   op2 = opcode[2]; op3 = opcode[3]; op4 = opcode[4]; op5 = opcode[5]; sw = NumWrite
endmodule

module IFU (
  input  clk,
  input  Reset,
  input  [31:0] PC_prime,
  output [31:0] Instr,
  output [31:0] PC
);

  wire [31:0] register_1_q, subtractor_1_out;

  Subtractor #(.width(32)) subtractor_1 (.a(PC_prime), .b(32'h3000), .out(subtractor_1_out));  // open: bin, bout
  Register #(.width(32)) register_1 (.D(subtractor_1_out), .Q(register_1_q), .clk(clk), .clr(Reset));  // open: en
  Adder #(.width(32)) adder_1 (.a(register_1_q), .b(32'h3000), .out(PC));  // open: cin, cout
  IM im_1 (.clk(clk), .Reset(Reset), .PC(PC), .Instr(Instr));
endmodule
