// Logisim project Pre_Logisim_fibonacci_1.circ as structural Verilog: 3 circuits, main circuit main
module main (
  input  [2:0] in_1,
  output [3:0] out_2
);

  wire count_1_out_2;
  wire [3:0] calculate_1_out_2;

  count count_1 (.in_1(in_1), .out_2(count_1_out_2));
  calculate calculate_1 (.in_1(count_1_out_2), .out_2(calculate_1_out_2));
  Multiplexer #(.width(4)) multiplexer_1 (
    .in0(4'b0000), .in1(calculate_1_out_2), .out(out_2), .sel(count_1_out_2));  // open: en
endmodule

module calculate (
  input  in_1,
  output [3:0] out_2
);

  wire clock_1_out, counter_1_q, not_1_out;
  wire [3:0] adder_1_out, multiplexer_1_out, prew;

  Counter #(.width(1), .max('h1), .ongoal("stay")) counter_1 (
    .Q(counter_1_q), .clk(clock_1_out));  // open: load, D, count, carry, clr
  Multiplexer #(.width(4)) multiplexer_1 (
    .in0(4'b0001), .in1(out_2), .out(multiplexer_1_out), .sel(counter_1_q));  // open: en
  not not_1 (not_1_out, in_1);
  Register #(.width(4)) register_1 (.D(multiplexer_1_out), .en(not_1_out), .Q(prew), .clk(clock_1_out));  // open: clr
  Clock clock_1 (.out(clock_1_out));
  Adder #(.width(4)) adder_1 (.a(prew), .b(out_2), .out(adder_1_out));  // open: cin, cout
  Register #(.width(4)) register_2 (.D(adder_1_out), .en(not_1_out), .Q(out_2), .clk(clock_1_out));  // open: clr

  // Other names for the same wires on the sheet: now[3:0] = out_2
endmodule

module count (
  input  [2:0] in_1,
  output out_2
);

  wire clock_1_out;
  wire [3:0] bit_extender_1_out, counter_1_q;

  assign bit_extender_1_out = {{1{1'b0}}, in_1};  // Bit_Extender bit_extender_1
  Counter #(.width(4), .max('hf), .ongoal("stay")) counter_1 (
    .Q(counter_1_q), .clk(clock_1_out));  // open: load, D, count, carry, clr
  Clock clock_1 (.out(clock_1_out));
  Comparator #(.width(4), .mode("unsigned")) comparator_1 (
    .a(bit_extender_1_out), .b(counter_1_q), .lt(out_2));  // open: gt, eq
endmodule
