// Logisim project Pre_Logisim_fibonacci_2.circ as structural Verilog: 8 circuits, main circuit main
module main (
  input  [31:0] Input,
  output [31:0] Output
);

  wire count_1_freeze, count_1_output_sign;

  Count count_1 (.Input(Input), .freeze(count_1_freeze), .Output_sign(count_1_output_sign));
  Calculate calculate_1 (.freeze(count_1_freeze), .Output_Sign(count_1_output_sign), .Output(Output));
endmodule

module Matrix_Memory (
  input  [31:0] a11_in,
  input  [31:0] a12_in,
  input  [31:0] a21_in,
  input  [31:0] a22_in,
  input  enable,
  input  clk,
  output [31:0] a11_out,
  output [31:0] a12_out,
  output [31:0] a21_out,
  output [31:0] a22_out
);

  Register #(.width(32)) a11 (.D(a11_in), .en(enable), .Q(a11_out), .clk(clk));  // open: clr
  Register #(.width(32)) a12 (.D(a12_in), .en(enable), .Q(a12_out), .clk(clk));  // open: clr
  Register #(.width(32)) a21 (.D(a21_in), .en(enable), .Q(a21_out), .clk(clk));  // open: clr
  Register #(.width(32)) a22 (.D(a22_in), .en(enable), .Q(a22_out), .clk(clk));  // open: clr
endmodule

module Matrix_Mult (
  input  [31:0] a11,
  input  [31:0] a12,
  input  [31:0] a21,
  input  [31:0] a22,
  input  [31:0] b11,
  input  [31:0] b12,
  input  [31:0] b21,
  input  [31:0] b22,
  output [31:0] c11,
  output [31:0] c12,
  output [31:0] c21,
  output [31:0] c22
);

  wire [31:0] multiplier_1_out, multiplier_2_out, multiplier_3_out, multiplier_4_out, multiplier_5_out,
       multiplier_6_out, multiplier_7_out, multiplier_8_out;

  Multiplier #(.width(32)) multiplier_1 (.a(a11), .b(b11), .out(multiplier_1_out));  // open: cin, cout
  Multiplier #(.width(32)) multiplier_2 (.a(a12), .b(b21), .out(multiplier_2_out));  // open: cin, cout
  Multiplier #(.width(32)) multiplier_3 (.a(a11), .b(b12), .out(multiplier_3_out));  // open: cin, cout
  Multiplier #(.width(32)) multiplier_4 (.a(a12), .b(b22), .out(multiplier_4_out));  // open: cin, cout
  Multiplier #(.width(32)) multiplier_5 (.a(a21), .b(b11), .out(multiplier_5_out));  // open: cin, cout
  Multiplier #(.width(32)) multiplier_6 (.a(a22), .b(b21), .out(multiplier_6_out));  // open: cin, cout
  Multiplier #(.width(32)) multiplier_7 (.a(a21), .b(b12), .out(multiplier_7_out));  // open: cin, cout
  Multiplier #(.width(32)) multiplier_8 (.a(a22), .b(b22), .out(multiplier_8_out));  // open: cin, cout
  Adder #(.width(32)) adder_1 (.a(multiplier_1_out), .b(multiplier_2_out), .out(c11));  // open: cin, cout
  Adder #(.width(32)) adder_2 (.a(multiplier_3_out), .b(multiplier_4_out), .out(c12));  // open: cin, cout
  Adder #(.width(32)) adder_3 (.a(multiplier_5_out), .b(multiplier_6_out), .out(c21));  // open: cin, cout
  Adder #(.width(32)) adder_4 (.a(multiplier_7_out), .b(multiplier_8_out), .out(c22));  // open: cin, cout
endmodule

module Matrix_Mux (
  input  [31:0] a11,
  input  [31:0] a12,
  input  [31:0] a21,
  input  [31:0] a22,
  input  [31:0] b11,
  input  [31:0] b12,
  input  [31:0] b21,
  input  [31:0] b22,
  input  in_9,
  output [31:0] out11,
  output [31:0] out12,
  output [31:0] out21,
  output [31:0] out22
);

  Multiplexer #(.width(32)) multiplexer_1 (.in0(a11), .in1(b11), .out(out11), .sel(in_9));  // open: en
  Multiplexer #(.width(32)) multiplexer_2 (.in0(a12), .in1(b12), .out(out12), .sel(in_9));  // open: en
  Multiplexer #(.width(32)) multiplexer_3 (.in0(a21), .in1(b21), .out(out21), .sel(in_9));  // open: en
  Multiplexer #(.width(32)) multiplexer_4 (.in0(a22), .in1(b22), .out(out22), .sel(in_9));  // open: en

  // Other names for the same wires on the sheet: select = in_9
endmodule

module Matrix_first_value (
  output [31:0] out11,
  output [31:0] out12,
  output [31:0] out21,
  output [31:0] out22
);


  assign out11 = 32'h1;
  assign out12 = 32'h1;
  assign out21 = 32'h1;
  assign out22 = {32{1'b0}};
endmodule

module Matrix_unit (
  output [31:0] out11,
  output [31:0] out12,
  output [31:0] out21,
  output [31:0] out22
);


  assign out11 = 32'h1;
  assign out12 = {32{1'b0}};
  assign out21 = {32{1'b0}};
  assign out22 = 32'h1;
endmodule

module Calculate (
  input  freeze,
  input  Output_Sign,
  output [31:0] Output
);

  wire clk, enable, init;
  wire [31:0] a11, a12, a21, a22, Matrix_first_value_out11, Matrix_first_value_out12,
       Matrix_first_value_out21, Matrix_first_value_out22, Matrix_Mult_2_c11, Matrix_Mult_2_c12,
       Matrix_Mult_2_c21, Matrix_Mult_2_c22, Matrix_Mult_c11, Matrix_Mult_c12, Matrix_Mult_c21,
       Matrix_Mult_c22, Matrix_Mux_2_out11, Matrix_Mux_2_out12, Matrix_Mux_2_out21, Matrix_Mux_2_out22,
       Matrix_Mux_3_out11, Matrix_Mux_3_out12, Matrix_Mux_3_out21, Matrix_Mux_3_out22, Matrix_Mux_out11,
       Matrix_Mux_out12, Matrix_Mux_out21, Matrix_Mux_out22, Matrix_unit_2_out11, Matrix_unit_2_out12,
       Matrix_unit_2_out21, Matrix_unit_2_out22, Matrix_unit_out11, Matrix_unit_out12, Matrix_unit_out21,
       Matrix_unit_out22, s11, s12, s21, s22;

  Matrix_unit Matrix_unit (
    .out11(Matrix_unit_out11), .out12(Matrix_unit_out12), .out21(Matrix_unit_out21), .out22(Matrix_unit_out22));
  Matrix_Mult Matrix_Mult (
    .a11(a11), .a12(a12), .a21(a21), .a22(a22), .b11(a11), .b12(a12), .b21(a21), .b22(a22),
    .c11(Matrix_Mult_c11), .c12(Matrix_Mult_c12), .c21(Matrix_Mult_c21), .c22(Matrix_Mult_c22));
  Matrix_Mux Matrix_Mux (
    .a11(Matrix_unit_out11), .a12(Matrix_unit_out12), .a21(Matrix_unit_out21), .a22(Matrix_unit_out22),
    .b11(a11), .b12(a12), .b21(a21), .b22(a22), .in_9(Output_Sign), .out11(Matrix_Mux_out11),
    .out12(Matrix_Mux_out12), .out21(Matrix_Mux_out21), .out22(Matrix_Mux_out22));
  Matrix_first_value Matrix_first_value (
    .out11(Matrix_first_value_out11), .out12(Matrix_first_value_out12), .out21(Matrix_first_value_out21),
    .out22(Matrix_first_value_out22));
  Matrix_Memory Matrix_Memory (
    .a11_in(Matrix_Mux_2_out11), .a12_in(Matrix_Mux_2_out12), .a21_in(Matrix_Mux_2_out21),
    .a22_in(Matrix_Mux_2_out22), .enable(enable), .clk(clk), .a11_out(a11), .a12_out(a12), .a21_out(a21),
    .a22_out(a22));
  Matrix_Mux Matrix_Mux_2 (
    .a11(Matrix_first_value_out11), .a12(Matrix_first_value_out12), .a21(Matrix_first_value_out21),
    .a22(Matrix_first_value_out22), .b11(Matrix_Mult_c11), .b12(Matrix_Mult_c12), .b21(Matrix_Mult_c21),
    .b22(Matrix_Mult_c22), .in_9(init), .out11(Matrix_Mux_2_out11), .out12(Matrix_Mux_2_out12),
    .out21(Matrix_Mux_2_out21), .out22(Matrix_Mux_2_out22));
  // Probe on nothing
  Matrix_unit Matrix_unit_2 (
    .out11(Matrix_unit_2_out11), .out12(Matrix_unit_2_out12), .out21(Matrix_unit_2_out21),
    .out22(Matrix_unit_2_out22));
  Matrix_Mult Matrix_Mult_2 (
    .a11(s11), .a12(s12), .a21(s21), .a22(s22), .b11(Matrix_Mux_out11), .b12(Matrix_Mux_out12),
    .b21(Matrix_Mux_out21), .b22(Matrix_Mux_out22), .c11(Matrix_Mult_2_c11), .c12(Matrix_Mult_2_c12),
    .c21(Matrix_Mult_2_c21), .c22(Matrix_Mult_2_c22));
  Matrix_Mux Matrix_Mux_3 (
    .a11(Matrix_unit_2_out11), .a12(Matrix_unit_2_out12), .a21(Matrix_unit_2_out21),
    .a22(Matrix_unit_2_out22), .b11(Matrix_Mult_2_c11), .b12(Matrix_Mult_2_c12), .b21(Matrix_Mult_2_c21),
    .b22(Matrix_Mult_2_c22), .in_9(init), .out11(Matrix_Mux_3_out11), .out12(Matrix_Mux_3_out12),
    .out21(Matrix_Mux_3_out21), .out22(Matrix_Mux_3_out22));
  Matrix_Memory Matrix_Memory_2 (
    .a11_in(Matrix_Mux_3_out11), .a12_in(Matrix_Mux_3_out12), .a21_in(Matrix_Mux_3_out21),
    .a22_in(Matrix_Mux_3_out22), .enable(enable), .clk(clk), .a11_out(s11), .a12_out(s12), .a21_out(s21),
    .a22_out(s22));
  Counter #(.width(1), .max('h1), .ongoal("stay")) counter_1 (.Q(init), .clk(clk));  // open: load, D, count, carry, clr
  Clock clock_1 (.out(clk));
  Multiplexer #(.width(32)) multiplexer_1 (.in0({32{1'b0}}), .in1(s12), .out(Output), .sel(freeze));  // open: en
  not not_1 (enable, freeze);
endmodule

module Count (
  input  [31:0] Input,
  output freeze,
  output Output_sign
);

  wire clock_1_out, comparator_1_eq, counter_1_q;
  wire [31:0] multiplexer_1_out, n, shifter_1_out;

  Counter #(.width(1), .max('h1), .ongoal("stay")) counter_1 (
    .Q(counter_1_q), .clk(clock_1_out));  // open: load, D, count, carry, clr
  Clock clock_1 (.out(clock_1_out));
  Shifter #(.width(32), .shift("lr")) shifter_1 (.in(n), .\dist (5'b00001), .out(shifter_1_out));
  Multiplexer #(.width(32)) multiplexer_1 (
    .in0(Input), .in1(shifter_1_out), .out(multiplexer_1_out), .sel(counter_1_q));  // open: en
  Register #(.width(32)) register_1 (.D(multiplexer_1_out), .Q(n), .clk(clock_1_out));  // open: en, clr
  Bit_Extender #(.in_width(32), .out_width(1)) bit_extender_1 (.in(n), .out(Output_sign));
  Multiplexer multiplexer_2 (.in0(1'b0), .in1(comparator_1_eq), .out(freeze), .sel(counter_1_q));  // open: en
  Comparator #(.width(32), .mode("unsigned")) comparator_1 (
    .a({32{1'b0}}), .b(n), .eq(comparator_1_eq));  // open: gt, lt
endmodule
