// Logisim project Pre_Logisim_mod5_Mealy.circ as structural Verilog: 3 circuits, main circuit mod5
module mod5 (
  input  In,
  output out_2,
  output out_3,
  output out_4,
  output out_5,
  output out_6
);

  wire clock_1_out;
  wire [1:0] register_1_q, \状态转移_1_c_1 ;

  \状态转移  \u_状态转移_1  (.c1(register_1_q[0]), .c2(register_1_q[1]), .In(In), .c_1(\状态转移_1_c_1 [0]), .c_2(\状态转移_1_c_1 [1]));
  Register #(.width(2)) register_1 (.D(\状态转移_1_c_1 ), .Q(register_1_q), .clk(clock_1_out));  // open: en, clr
  Clock clock_1 (.out(clock_1_out));
  \状态输出  \u_状态输出_1  (
    .c_1(register_1_q[0]), .c_2(register_1_q[1]), .In(In), .s0(out_2), .s1(out_3), .s2(out_4), .s3(out_5),
    .s4(out_6));
endmodule

module \状态转移  (
  input  c1,
  input  c2,
  input  In,
  output c_1,
  output c_2
);

  wire and_1_out, and_2_out, and_3_out, and_4_out, and_5_out, and_6_out, not_1_out, not_2_out, not_3_out,
       not_4_out, not_5_out, not_6_out, not_7_out, not_8_out;

  not not_1 (not_1_out, c1);
  not not_2 (not_2_out, c2);
  not not_3 (not_3_out, c1);
  not not_4 (not_4_out, c2);
  not not_5 (not_5_out, c1);
  not not_6 (not_6_out, In);
  not not_7 (not_7_out, c2);
  not not_8 (not_8_out, In);
  and and_1 (and_1_out, not_1_out, c2);
  and and_2 (and_2_out, c1, not_2_out);
  and and_3 (and_3_out, not_3_out, not_4_out, In);
  and and_4 (and_4_out, not_5_out, c2, not_6_out);
  and and_5 (and_5_out, c1, not_7_out, not_8_out);
  and and_6 (and_6_out, c1, c2, In);
  or or_1 (c_1, and_1_out, and_2_out);
  or or_2 (c_2, and_3_out, and_4_out, and_5_out, and_6_out);
endmodule

module \状态输出  (
  input  c_1,
  input  c_2,
  input  In,
  output s0,
  output s1,
  output s2,
  output s3,
  output s4
);

  wire and_1_out, and_2_out, and_3_out, and_4_out, and_5_out, and_6_out, and_7_out, and_8_out, not_1_out,
       not_2_out, not_3_out, not_4_out, not_5_out, not_6_out, not_7_out, not_8_out, not_9_out, not_10_out,
       not_11_out, not_12_out;

  not not_1 (not_1_out, c_1);
  not not_2 (not_2_out, c_2);
  not not_3 (not_3_out, In);
  not not_4 (not_4_out, In);
  not not_5 (not_5_out, c_1);
  not not_6 (not_6_out, c_2);
  not not_7 (not_7_out, c_1);
  not not_8 (not_8_out, c_2);
  not not_9 (not_9_out, c_1);
  not not_10 (not_10_out, In);
  not not_11 (not_11_out, c_2);
  not not_12 (not_12_out, In);
  and and_1 (and_1_out, not_1_out, not_2_out, not_3_out);
  and and_2 (and_2_out, c_1, c_2, not_4_out);
  and and_3 (and_3_out, not_5_out, not_6_out, In);
  and and_4 (and_4_out, c_1, c_2, In);
  and and_5 (and_5_out, not_7_out, c_2, In);
  and and_6 (and_6_out, c_1, not_8_out, In);
  and and_7 (and_7_out, not_9_out, c_2, not_10_out);
  and and_8 (and_8_out, c_1, not_11_out, not_12_out);
  or or_1 (s1, and_1_out, and_2_out);
  or or_2 (s2, and_3_out, and_4_out);
  or or_3 (s3, and_5_out, and_6_out);
  or or_4 (s4, and_7_out, and_8_out);

  assign s0 = 1'b0;
endmodule
