// Logisim project Pre_Logisim_mod5_Moore.circ as structural Verilog: 1 circuit, main circuit mod5
module mod5 (
  input  In,
  output S0,
  output S1,
  output S2,
  output S3,
  output S4
);

  wire clock_1_out, not_1_out, xor_1_out;
  wire [1:0] multiplexer_1_out, state;

  xor xor_1 (xor_1_out, state[0], state[1]);
  Multiplexer #(.width(2)) multiplexer_1 (.in0(2'b11), .in1(2'b10), .out(multiplexer_1_out), .sel(In), .en(xor_1_out));
  not not_1 (not_1_out, xor_1_out);
  Multiplexer #(.width(2)) multiplexer_2 (.in0(2'b00), .in1(2'b01), .out(multiplexer_1_out), .sel(In), .en(not_1_out));
  Clock clock_1 (.out(clock_1_out));
  Register #(.width(2)) register_1 (.D(multiplexer_1_out), .Q(state), .clk(clock_1_out));  // open: en, clr
  not not_2 (S0, 1'b1);
  Demultiplexer #(.select(2), .enable("false")) demultiplexer_1 (
    .out0(S1), .out1(S2), .out2(S3), .out3(S4), .in(1'b1), .sel(multiplexer_1_out));
endmodule
